# Fritzing sketch Sleep_Sensei_PCB (saved by Fritzing 0.8.5b)
circuit board: 4.99613cm x 3.78567cm
breadboards: 1

parts:
  U1 = attiny85 [package=dip]
  3V_DC = Battery
  C2 = Electrolytic Capacitor [capacitance=1µF package="0405 [SMD, electrolytic]"]
  LED1 = LED - 5mm [color="Blue (525nm)" package="5 mm [THT]"]
  LED2 = LED - 5mm [color="Blue (525nm)" package="5 mm [THT]"]
  LED3 = LED - 5mm [color="Blue (525nm)" package="5 mm [THT]"]
  LED4 = LED - 5mm [color="Blue (525nm)" package="5 mm [THT]"]
  C1 = Electrolytic Capacitor [capacitance=1µF package="100 mil [THT, electrolytic]"]
  R1 = Resistor [tolerance=±5% resistance=10k package=THT]
  R2 = Resistor [tolerance=±5% resistance=10k package=THT]
  R3 = Resistor [tolerance=±5% resistance=220 package=THT]
  R5 = Resistor [tolerance=±5% resistance=10k package="0603 [SMD]"]
  R4 = Resistor [tolerance=±5% resistance=10k package="0603 [SMD]"]
  R6 = Resistor [tolerance=±5% resistance=220 package="0603 [SMD]"]
  ENCODER1 = Rotary Encoder with Knob
  J1 = female pin header, 4 pins [form="♀ (female)"]

nets:
  N1: U1.Pin_1, J1.pin1
  N2: U1.Pin_2, R1.Pin_1, R5.Pin_1, ENCODER1.no_name_yet#3
  N3: U1.Pin_3, R2.Pin_1, R4.Pin_1, ENCODER1.no_name_yet#1
  N4: U1.Pin_4, 3V_DC.-, C2.+, LED1.cathode, LED2.cathode, LED3.cathode, LED4.cathode, C1.-, R3.Pin_1, R6.Pin_1, ENCODER1.no_name_yet#2
  N5: U1.Pin_5, LED1.anode, LED2.anode, LED3.anode, LED4.anode, J1.pin4
  N6: U1.Pin_6, R3.Pin_0, R6.Pin_0, ENCODER1.no_name_yet#5, J1.pin3
  N7: U1.Pin_7, J1.pin2
  N8: U1.Pin_8, 3V_DC.+, C2.-, C1.+, R1.Pin_0, R2.Pin_0, R5.Pin_0, R4.Pin_0, ENCODER1.no_name_yet#4

notes:
  Sleep Sensei
  getsleepsensei.com
  github.com/jerwil/SleepCoach
  220Ω
  10KΩ
  10 μF

custom parts:
  Rotary Encoder with Knob: Rotary Encoder with 1/4" Shaft and Knob
