# Fritzing sketch Sleep_Sensei_SMD (saved by Fritzing 0.9.1b)
circuit board: 4.99613cm x 3.78567cm
breadboards: 1

parts:
  3V_DC = Battery
  C1 = Electrolytic Capacitor [capacitance=1µF package="0405 [SMD, electrolytic]"]
  LED1 = LED - 5mm [color="Blue (525nm)" package="5 mm [THT]"]
  LED2 = LED - 5mm [color="Blue (525nm)" package="5 mm [THT]"]
  LED3 = LED - 5mm [color="Blue (525nm)" package="5 mm [THT]"]
  LED4 = LED - 5mm [color="Blue (525nm)" package="5 mm [THT]"]
  ENCODER1 = Rotary Encoder with Knob
  part = female pin header, 4 pins [form="♀ (female)"]  # not connected
  U1 = ATTINY13 [package=so]
  R1 = Resistor [tolerance=±5% resistance=220 package="0603 [SMD]"]
  R3 = Resistor [tolerance=±5% resistance=10k package="0603 [SMD]"]
  R2 = Resistor [tolerance=±5% resistance=10k package="0603 [SMD]"]

nets:
  N1: 3V_DC.-, C1.+, LED1.cathode, LED2.cathode, LED3.cathode, LED4.cathode, ENCODER1.no_name_yet#2, U1.GND, R1.Pin_1
  N2: 3V_DC.+, C1.-, ENCODER1.no_name_yet#4, U1.VCC, R3.Pin_0, R2.Pin_0
  N3: LED1.anode, LED2.anode, LED3.anode, LED4.anode, U1.PB0(MOSI)
  N4: ENCODER1.no_name_yet#1, U1.PB4(ADC2), R3.Pin_1
  N5: ENCODER1.no_name_yet#3, U1.PB3(ADC3), R2.Pin_1
  N6: ENCODER1.no_name_yet#5, U1.PB1(MISO), R1.Pin_0

notes:
  Sleep Sensei
  getsleepsensei.com
  github.com/jerwil/SleepCoach
  10KΩ
  10 μF
  220Ω

custom parts:
  Rotary Encoder with Knob: Rotary Encoder with 1/4" Shaft and Knob
